// Logisim project Signal.circ as structural Verilog
module SR_Latch (
  input  R,
  input  S,
  output Q,
  output Not_Q
);

  wire or_1_out, or_2_out;

  or or_1 (or_1_out, R, Not_Q);
  not not_1 (Q, or_1_out);
  or or_2 (or_2_out, Q, S);
  not not_2 (Not_Q, or_2_out);
endmodule
